// Logisim project Decodificadorr.circ as structural Verilog: 3 circuits, main circuit decodificador
module decodificador (
  input  [31:0] Instrucao,
  output [4:0] rd,
  output [5:0] opcode,
  output [2:0] funct3,
  output [4:0] rs1,
  output [4:0] rs2,
  output [31:0] Imediato
);

  wire [2:0] i_out;
  wire [31:0] imm_b_saida, imm_i_saida, imm_s_saida;

  extensorSinal_11 imm_s (.Entrada({Instrucao[31:26], Instrucao[6:2]}), .Saida(imm_s_saida));
  extensorSinal_12 imm_b (.Entrada({Instrucao[31:26], Instrucao[6:2], 1'b0}), .Saida(imm_b_saida));
  extensorSinal_11 imm_i (.Entrada(Instrucao[31:21]), .Saida(imm_i_saida));
  and i (i_out[0], ~Instrucao[7], ~Instrucao[8], Instrucao[9], ~Instrucao[10], ~Instrucao[11], ~Instrucao[12]);  // AND_Gate
  and s (i_out[1], ~Instrucao[7], Instrucao[8], ~Instrucao[9], ~Instrucao[10], ~Instrucao[11], ~Instrucao[12]);  // AND_Gate
  and b (i_out[2], ~Instrucao[7], ~Instrucao[8], ~Instrucao[9], Instrucao[10], Instrucao[11], ~Instrucao[12]);  // AND_Gate
  Multiplexer #(.select(3), .width(32)) multiplexer_1 (
    .in1(imm_i_saida), .in2(imm_s_saida), .in4(imm_b_saida), .out(Imediato), .sel(i_out));  // open: in0, in3, in5, in6, in7

  assign funct3 = Instrucao[15:13];
  assign opcode = Instrucao[12:7];
  assign rd = Instrucao[6:2];
  assign rs1 = Instrucao[20:16];
  assign rs2 = Instrucao[25:21];
endmodule

module extensorSinal_11 (
  input  [10:0] Entrada,
  output [31:0] Saida
);


  assign Saida = {{22{Entrada[10]}}, Entrada[9:0]};
endmodule

module extensorSinal_12 (
  input  [11:0] Entrada,
  output [31:0] Saida
);


  assign Saida = {{21{Entrada[11]}}, Entrada[10:0]};
endmodule
