// Logisim project MemInstruc.circ as structural Verilog: 1 circuit, main circuit Men_Instruct
module Men_Instruct (
  input  [31:0] pc,
  output [31:0] instrucao
);

  ROM #(.addrWidth(24), .dataWidth(32)) rom_1 (.addr(pc[25:2]), .data(instrucao));
endmodule
