// Logisim project ULA.circ as structural Verilog: 4 circuits, main circuit Shift
module ULA (
  input  [31:0] A,
  input  [31:0] B,
  input  [2:0] ALUControl,
  output sZero,
  output [31:0] Result
);

  wire comparator_1_lt;
  wire [4:0] shift_1_shiftout, shift_2_shiftout;
  wire [31:0] adder_1_out, and_1_out, extensorsinal_1_eout, or_1_out, shifter_1_out, shifter_2_out,
       subtractor_1_out, xor_1_out;

  assign and_1_out = A & B;  // AND_Gate and_1, 32 bits wide
  assign or_1_out = A | B;  // OR_Gate or_1, 32 bits wide
  Shift shift_1 (.Entrada(B), .ShiftOut(shift_1_shiftout));
  Shift shift_2 (.Entrada(B), .ShiftOut(shift_2_shiftout));
  Adder #(.width(32)) adder_1 (.a(A), .b(B), .out(adder_1_out));  // open: cin, cout
  Subtractor #(.width(32)) subtractor_1 (.a(A), .b(B), .out(subtractor_1_out));  // open: bin, bout
  Comparator #(.width(32)) comparator_1 (.a(A), .b(B), .lt(comparator_1_lt));  // open: gt, eq
  ExtensorSinal extensorsinal_1 (.EIn(comparator_1_lt), .EOut(extensorsinal_1_eout));
  assign xor_1_out = A ^ B;  // XOR_Gate xor_1, 32 bits wide
  Shifter #(.width(32)) shifter_1 (.in(A), .\dist (shift_1_shiftout), .out(shifter_1_out));
  Shifter #(.shift("lr"), .width(32)) shifter_2 (.in(A), .\dist (shift_2_shiftout), .out(shifter_2_out));
  zero zero_1 (.ZIn(Result), .ZOut(sZero));
  Multiplexer #(.select(3), .width(32)) multiplexer_1 (
    .in0(adder_1_out), .in1(subtractor_1_out), .in2(and_1_out), .in3(extensorsinal_1_eout), .in4(or_1_out),
    .in5(xor_1_out), .in6(shifter_1_out), .in7(shifter_2_out), .out(Result), .sel(ALUControl));
endmodule

module ExtensorSinal (
  input  EIn,
  output [31:0] EOut
);


  assign EOut = {{31{1'b0}}, EIn};
endmodule

module Shift (
  input  [31:0] Entrada,
  output [4:0] ShiftOut
);


  assign ShiftOut = Entrada[4:0];
endmodule

module zero (
  input  [31:0] ZIn,
  output ZOut
);

  Comparator #(.width(32)) comparator_1 (.a(ZIn), .b({32{1'b0}}), .eq(ZOut));  // open: gt, lt
endmodule
