// Logisim project uc_Principal.circ as structural Verilog: 1 circuit, main circuit ucPrincipal
module ucPrincipal (
  input  [5:0] in_1,
  output ALUSrc,
  output RegWrite,
  output MemToReg,
  output MemRead,
  output Branch,
  output MemWrite
);

  wire I_out, R_out;

  and R (R_out, ~in_1[0], ~in_1[1], in_1[2], in_1[3], ~in_1[4], ~in_1[5]);  // AND_Gate
  and I (I_out, in_1[0], in_1[1], ~in_1[2], in_1[3], in_1[4], in_1[5]);  // AND_Gate
  and Load (MemRead, in_1[0], ~in_1[1], ~in_1[2], ~in_1[3], ~in_1[4], ~in_1[5]);  // AND_Gate
  and S (MemWrite, ~in_1[0], in_1[1], ~in_1[2], ~in_1[3], ~in_1[4], ~in_1[5]);  // AND_Gate
  and B (Branch, ~in_1[0], ~in_1[1], ~in_1[2], in_1[3], in_1[4], ~in_1[5]);  // AND_Gate
  or or_1 (ALUSrc, I_out, MemRead, MemWrite);
  or or_2 (RegWrite, R_out, I_out, MemRead);

  assign MemToReg = MemRead;
endmodule
