// Logisim project d09.circ as structural Verilog: 1 circuit, main circuit main
module main (
);

  wire and_1_out, clock_1_out, ucprincipal_1_alusrc, ucprincipal_1_branch, ucprincipal_1_memread,
       ucprincipal_1_memtoreg, ucprincipal_1_memwrite, ucprincipal_1_regwrite;
  wire [2:0] decodificador_1_funct3;
  wire [4:0] decodificador_1_rd, decodificador_1_rs1, decodificador_1_rs2;
  wire [5:0] decodificador_1_opcode;
  wire [31:0] adder_1_out, adder_2_out, bancoregistradores_1_ld1, bancoregistradores_1_ld2,
       decodificador_1_imediato, men_instruct_1_instrucao, multiplexer_1_out, multiplexer_2_out, PC_q,
       ula_1_result, undriven;

  Clock clock_1 (.out(clock_1_out));
  Register #(.width(32)) PC (.D(multiplexer_1_out), .clk(clock_1_out), .Q(PC_q));  // open: en, clr
  Adder #(.width(32)) adder_1 (.a(PC_q), .b(32'h4), .out(adder_1_out));  // open: cin, cout
  Multiplexer #(.width(32)) multiplexer_1 (
    .in0(adder_1_out), .in1(adder_2_out), .out(multiplexer_1_out), .sel(and_1_out));
  Adder #(.width(32)) adder_2 (.a(decodificador_1_imediato), .b(PC_q), .out(adder_2_out));  // open: cin, cout
  Men_Instruct men_instruct_1 (.pc(PC_q), .instrucao(men_instruct_1_instrucao));
  and and_1 (and_1_out, ucprincipal_1_branch, 1'b0);
  decodificador decodificador_1 (
    .Instrucao(men_instruct_1_instrucao), .rd(decodificador_1_rd), .opcode(decodificador_1_opcode),
    .funct3(decodificador_1_funct3), .rs1(decodificador_1_rs1), .rs2(decodificador_1_rs2),
    .Imediato(decodificador_1_imediato));
  ucPrincipal ucprincipal_1 (
    .in_1(decodificador_1_opcode), .ALUSrc(ucprincipal_1_alusrc), .RegWrite(ucprincipal_1_regwrite),
    .MemToReg(ucprincipal_1_memtoreg), .MemRead(ucprincipal_1_memread), .Branch(ucprincipal_1_branch),
    .MemWrite(ucprincipal_1_memwrite));
  bancoRegistradores bancoregistradores_1 (
    .WR(decodificador_1_rd), .RegWrite(ucprincipal_1_regwrite), .LR1(decodificador_1_rs1),
    .LR2(decodificador_1_rs2), .clk(clock_1_out), .LD1(bancoregistradores_1_ld1),
    .LD2(bancoregistradores_1_ld2));  // open: WD
  Multiplexer #(.width(32)) multiplexer_2 (
    .in0(bancoregistradores_1_ld2), .in1(decodificador_1_imediato), .out(multiplexer_2_out),
    .sel(ucprincipal_1_alusrc));
  ULA ula_1 (
    .B(multiplexer_2_out), .ALUControl(decodificador_1_funct3), .A(bancoregistradores_1_ld1),
    .Result(ula_1_result));  // open: sZero
  Multiplexer #(.width(32)) multiplexer_3 (
    .in0(ula_1_result), .in1(undriven), .sel(ucprincipal_1_memtoreg));  // open: out
endmodule
